# Fritzing sketch pcb-ok-ultrasonic+wi-fi (saved by Fritzing 0.9.3b)
circuit board: 6cm x 6cm
breadboards: 1

parts:
  Part1 = Arduino Nano (Rev3.0) (ICSP)
  J2 = screw terminal, 3 pins
  J3 = screw terminal, 4 pins
  C3 = Electrolytic Capacitor [capacitance=100µF package="100 mil [THT, electrolytic]"]
  J4 = screw terminal, 5 pins
  C4 = Electrolytic Capacitor [capacitance=1µF package="100 mil [THT, electrolytic]"]
  Q1 = PNP-Transistor [package="TO92 [THT]"]
  C5 = Ceramic Capacitor [capacitance=100nF package="100 mil [THT, multilayer]"]
  C6 = Ceramic Capacitor [capacitance=100nF package="100 mil [THT, multilayer]"]
  J5 = Screw terminal - 2 pins [package=THT]
  J6 = Screw terminal - 2 pins [package=THT]
  Pololu_A1 = Pololu A4988 [package=SO16]
  J7 = shrouded pin header, 8 pins [form="♂ (shrouded male)"]
  J8 = screw terminal, 4 pins

nets (from the pcb view):
  N1: Part1.D1/TX, J7.pin1
  N2: Part1.D0/RX, J7.pin5
  N3: Part1.GND, J2.pin1, J4.pin3, C4.-, J6.pin1, Pololu_A1.GND#8, J7.pin2, J7.pin4, J8.pin1
  N4: Part1.D2, Pololu_A1.DIR
  N5: Part1.D3, Pololu_A1.STEP
  N6: Part1.D4, Pololu_A1.ENABLE
  N7: Part1.D5, J2.pin2
  N8: Part1.D7, J8.pin2
  N9: Part1.D8, J8.pin3
  5V: Part1.5V, J2.pin3, C4.+, J6.pin2, Pololu_A1.VDD, J8.pin4
  N10: Part1.A5, J4.pin4
  N11: Part1.A4, J4.pin5
  N12: Part1.3V3, J7.pin6, J7.pin8
  N13: J3.pin1, Pololu_A1.2B
  N14: J3.pin2, Pololu_A1.2A
  N15: J3.pin3, Pololu_A1.1A
  N16: J3.pin4, Pololu_A1.1B
  N17: C3.-, J4.pin1, Q1.B, C5.1, C6.0, J5.pin1, Pololu_A1.GND#14
  N18: C3.+, Q1.C, C6.1, J5.pin2, Pololu_A1.VMOT
  N19: J4.pin2, Q1.E, C5.0
  N20: Pololu_A1.RESET, Pololu_A1.SLEEP
